# Fritzing sketch Home_Automation_ESPAlexa_LEDs (saved by Fritzing 0.9.3b)
breadboards: 1

parts:
  U2 = NodeMCU V1.0
  LED1 = smd LED [color="Red (633nm)" package="0603 [SMD]"]
  LED2 = smd LED [color="Green (560nm)" package="0603 [SMD]"]
  LED3 = smd LED [color="Blue (470nm)" package="0603 [SMD]"]
  LED4 = smd LED [color="Yellow (595nm)" package="0603 [SMD]"]
  R1 = Resistor [tolerance=±5% resistance=220 package="1206 [SMD]"]
  R2 = Resistor [tolerance=±5% resistance=220 package="1206 [SMD]"]
  R3 = Resistor [tolerance=±5% resistance=220 package="1206 [SMD]"]
  R4 = Resistor [tolerance=±5% resistance=220 package="1206 [SMD]"]

nets:
  N1: U2.D1, LED1.anode
  N2: U2.D2, LED2.anode
  N3: U2.GND, R1.Pin_0, R2.Pin_0, R3.Pin_0, R4.Pin_0
  N4: U2.D5, LED3.anode
  N5: U2.D6, LED4.anode
  N6: LED1.cathode, R1.Pin_1
  N7: LED2.cathode, R2.Pin_1
  N8: LED3.cathode, R3.Pin_1
  N9: LED4.cathode, R4.Pin_1

notes:
  LIVING ROOM
  BED ROOM

custom parts:
  NodeMCU V1.0: ESP8266 based NodeMCU
